# Fritzing sketch Weather_Station (saved by Fritzing 0.9.3b)
breadboards: 1

parts:
  U1 = ESP32S-HiLetgo [part_number=ESP32S-HiLetgo]
  OLED_I2C1 = OLED 128x64 I2C Monochrome Display
  R1 = Resistor [tolerance=±5% resistance=220 package=THT]
  R2 = Resistor [tolerance=±5% resistance=220 package=THT]
  LED1 = LED - 5mm [color="Red (633nm)" package="5 mm [THT]"]
  LED2 = LED - 5mm [color="Red (633nm)" package="5 mm [THT]"]

nets:
  GND: U1.GND, OLED_I2C1.GND
  VIN: U1.VIN, OLED_I2C1.VDD
  N1: U1.GPIO2, R1.Pin_1
  N2: U1.GPIO5, R2.Pin_1
  N3: U1.GPIO21, OLED_I2C1.SDA
  N4: U1.GPIO22, OLED_I2C1.SCK
  N5: R1.Pin_0, LED1.cathode
  N6: R2.Pin_0, LED2.cathode
  N7: LED1.anode, LED2.anode

custom parts:
  ESP32S-HiLetgo: HiLetgo ESP-WROOM-32 ESP32 ESP-32S Development Board 2.4GHz Dual-Mode WiFi + Bluetooth Dual Cores Microcontroller The ESP32 integrated with Antenna switches, RF Balun, power amplifiers, low-noise amplifiers, filters, and management modules, and the entire solution occupies the least area of PCB. 2.4 GHz Wi-Fi plus Bluetooth dual-mode chip, with TSMC Ultra-low power consumption 40nm technology,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
